// Logisim project COA project.circ as structural Verilog: 9 circuits, main circuit 4 bit a>b
module _4_bit_a_b (
  input  [4:0] input_A,
  input  [4:0] input_B,
  output out_3,
  output [1:0] out_4
);

  wire A___B_out, and_1_out, and_2_out, and_3_out, and_4_out, and_5_out, n4_bit_a_b_1_out_3, not_1_out,
       not_2_out, not_3_out, not_4_out, not_5_out, not_6_out, xor_1_out, xor_2_out, xor_3_out, xor_4_out;

  xor xor_1 (xor_1_out, input_A[3], input_B[3]);
  not not_1 (not_1_out, xor_1_out);
  xor xor_2 (xor_2_out, input_A[2], input_B[2]);
  not not_2 (not_2_out, xor_2_out);
  xor xor_3 (xor_3_out, input_A[1], input_B[1]);
  not not_3 (not_3_out, xor_3_out);
  xor xor_4 (xor_4_out, input_A[0], input_B[0]);
  and and_1 (and_1_out, input_A[3], xor_1_out);
  _4_bit_A_B u_4_bit_a_b_1 (.in_1(input_A), .in_2(input_B), .out_3(n4_bit_a_b_1_out_3));
  and and_2 (and_2_out, not_1_out, input_A[2], xor_2_out);
  and and_3 (and_3_out, not_1_out, not_2_out, input_A[1], xor_3_out);
  and and_4 (and_4_out, not_1_out, not_2_out, not_3_out, xor_4_out, input_A[0]);
  not not_4 (not_4_out, n4_bit_a_b_1_out_3);
  or A___B (A___B_out, and_1_out, and_2_out, and_3_out, and_4_out);
  not not_5 (not_5_out, A___B_out);
  not not_6 (not_6_out, 1'b1);
  and and_5 (and_5_out, not_5_out, not_4_out);
  Multiplexer #(.select(2)) multiplexer_1 (
    .in0(A___B_out), .in1(1'b1), .in2(not_6_out), .in3(and_5_out), .out(out_3),
    .sel({input_A[4], input_B[4]}), .en(1'b1));

  assign out_4 = {input_A[4], input_B[4]};
endmodule

module _4_bit_a_b_2 (
  input  [3:0] in_1,
  input  [3:0] in_2,
  output out_3
);

  wire and_1_out, and_2_out, and_3_out, and_4_out, not_1_out, not_2_out, not_3_out, xor_1_out, xor_2_out,
       xor_3_out, xor_4_out;

  xor xor_1 (xor_1_out, in_1[3], in_2[3]);
  not not_1 (not_1_out, xor_1_out);
  xor xor_2 (xor_2_out, in_1[2], in_2[2]);
  not not_2 (not_2_out, xor_2_out);
  xor xor_3 (xor_3_out, in_1[1], in_2[1]);
  not not_3 (not_3_out, xor_3_out);
  xor xor_4 (xor_4_out, in_1[0], in_2[0]);
  and and_1 (and_1_out, in_2[3], xor_1_out);
  and and_2 (and_2_out, not_1_out, in_2[2], xor_2_out);
  and and_3 (and_3_out, not_1_out, not_2_out, in_2[1], xor_3_out);
  and and_4 (and_4_out, not_1_out, not_2_out, not_3_out, xor_4_out, in_2[0]);
  or or_1 (out_3, and_1_out, and_2_out, and_3_out, and_4_out);
endmodule

module combined (
  input  [3:0] A,
  input  [3:0] B,
  output A_B,
  output A_B_2,
  output A_B_3
);

  // _4_bit_a_b 4_bit_a_b_1: pin names not known; wires that end beside it: A, B, A_B
  // _4_bit_a_b 4_bit_a_b_2: pin names not known; wires that end beside it: B, A, A_B_3
  nor nor_1 (A_B_2, A_B, A_B_3);

  // Notes on the sheet:
  //   A>B
  //   reversed the wiring
endmodule

module memory (
  input  [3:0] INPUT,
  input  in_2,
  input  in_3,
  output [3:0] OUTPUT
);

  wire and_1_out, n4_bit_a_b_1_p3;

  and and_1 (and_1_out, n4_bit_a_b_1_p3, in_2);
  Register #(.width(4), .trigger("high")) register_1 (.D(INPUT), .en(1'b1), .Q(OUTPUT), .clk(and_1_out), .clr(in_3));
  // _4_bit_a_b 4_bit_a_b_1: pin names not known; wires that end beside it: INPUT, OUTPUT, n4_bit_a_b_1_p3
endmodule

module FINAL (
  input  [3:0] INPUT,
  output [3:0] GREATEST_NUMBER
);

  wire button_1_out, RESET_out;

  Button button_1 (.out(button_1_out));
  memory memory_1 (.INPUT(INPUT), .OUTPUT(GREATEST_NUMBER), .in_3(RESET_out), .in_2(button_1_out));
  Button RESET (.out(RESET_out));
endmodule

module _0_and_1_LED (
  input  in_1
);

  wire decoder_1_out0, decoder_1_out1, or_1_out, or_2_out, or_4_out, or_5_out, or_6_out;

  Decoder #(.disabled(0), .enable("false")) decoder_1 (.out0(decoder_1_out0), .out1(decoder_1_out1), .sel(in_1));
  buf or_1 (or_1_out, decoder_1_out0);  // OR_Gate
  buf or_2 (or_2_out, decoder_1_out0);  // OR_Gate
  buf or_3 (or_2_out, decoder_1_out0);  // OR_Gate
  or or_4 (or_4_out, decoder_1_out0, or_1_out);
  or or_5 (or_5_out, decoder_1_out0, decoder_1_out1);
  or or_6 (or_6_out, decoder_1_out0, decoder_1_out1);
  _7_Segment_Display u_7_segment_display_1 (
    .f(or_4_out), .a(or_1_out), .b(or_5_out), .e(or_2_out), .d(or_2_out), .c(or_6_out));  // open: g, dp
endmodule

module decreasing_counter (
  input  in_1,
  input  [3:0] in_2,
  input  in_3,
  output [3:0] out_4,
  output out_5
);

  wire and_1_out, button_1_out, button_2_out, clock_1_out, not_1_out, or_1_out;

  Clock clock_1 (.out(clock_1_out));
  Button button_1 (.out(button_1_out));
  and and_1 (and_1_out, in_3, in_1, clock_1_out, not_1_out);
  not not_1 (not_1_out, out_5);
  Counter #(.width(4), .max('hf), .ongoal("stay")) counter_1 (
    .load(in_1), .D(in_2), .count(in_3), .Q(out_4), .carry(out_5), .clk(or_1_out), .clr(button_2_out));
  or or_1 (or_1_out, button_1_out, and_1_out);
  Button button_2 (.out(button_2_out));
endmodule

module ram_and_counter (
  input  in_1,
  input  [3:0] in_2,
  input  in_3,
  input  [3:0] in_4,
  output out_5,
  output [3:0] out_6
);

  wire and_1_out, button_1_out, button_2_out, button_3_out, clock_1_out, comparator_1_lt, not_1_out,
       not_2_out, or_1_out, or_2_out;
  wire [3:0] counter_1_q, ram_1_data;

  Clock clock_1 (.out(clock_1_out));
  not not_1 (not_1_out, out_5);
  Button button_1 (.out(button_1_out));
  and and_1 (and_1_out, in_3, in_1, not_1_out, clock_1_out);
  or or_1 (or_1_out, button_1_out, and_1_out);
  Counter #(.width(4), .max('hf), .ongoal("stay")) counter_1 (
    .load(in_1), .D(in_2), .count(in_3), .Q(counter_1_q), .carry(out_5), .clk(or_1_out), .clr(button_2_out));
  Button button_2 (.out(button_2_out));
  not not_2 (not_2_out, in_1);
  RAM #(.addrWidth(4), .dataWidth(4), .bus("separate")) ram_1 (
    .addr(counter_1_q), .din(in_4), .data(ram_1_data), .str(not_2_out), .sel(1'b1), .clk(or_1_out),
    .ld(in_1), .clr(button_2_out));
  Comparator #(.width(4), .mode("unsigned")) comparator_1 (
    .a(out_6), .b(ram_1_data), .lt(comparator_1_lt));  // open: gt, eq
  Button button_3 (.out(button_3_out));
  Register #(.width(4), .trigger("high")) register_1 (
    .D(ram_1_data), .en(1'b1), .Q(out_6), .clk(comparator_1_lt), .clr(or_2_out));
  or or_2 (or_2_out, button_2_out, button_3_out);
endmodule

module _4_bit_A_B (
  input  [4:0] in_1,
  input  [4:0] in_2,
  output out_3
);

  wire [4:0] xnor_1_out;

  assign xnor_1_out = ~(in_1 ^ in_2);  // XNOR_Gate xnor_1, 5 bits wide
  and and_1 (out_3, xnor_1_out[0], xnor_1_out[1], xnor_1_out[2], xnor_1_out[3], xnor_1_out[4]);
endmodule
